# Fritzing sketch Wiring (saved by Fritzing 0.9.6b)

parts:
  Mod1 = KY-015 Temperature & Humidity Sensor Module [package="Breakout board"]
  IC1 = DIP - 28 pins [chip_label=IC package="DIP (Dual Inline) [THT]"]

nets:
  N1: Mod1.S, IC1.P23
  VIN: Mod1.Vin, IC1.3V3
  N2: Mod1.-, IC1.GND

custom parts:
  KY-015 Temperature & Humidity Sensor Module: KY-015 temperature and humidity sensor module, provides a low-latency serial interface to measure humidity and temperature.
  DIP - 28 pins: A DIP stand-in part for whatever IC you want. With 28 pins on a 300mil dual inline package (DIP) footprint.
